# Fritzing sketch motherboard (saved by Fritzing 1.0.8)
breadboards: 1

parts:
  Mod1 = Raspberry Pi Pico
  Adafruit_DC_Power_BFF1 = Adafruit DC Power BFF [mn=Adafruit mpn=#5882 part_number=#5882]
  J1 = male pin header, 8 pins [form="♂ (male)"]
  R1 = Resistor [tolerance=±5% power=0.25W resistance=10k package=THT]
  D1 = Small signal Diode flat 300mil [part_number=1N4148 package="300 mil [THT]"]

nets:
  N1: Mod1.pin_1, J1.pin5
  N2: Mod1.pin_2, J1.pin4
  N3: Mod1.pin_3, Mod1.pin_8, Mod1.pin_13, Mod1.pin_28, Mod1.pin_33, Mod1.pin_38, Adafruit_DC_Power_BFF1.GND, J1.pin8
  N4: Mod1.pin_4, J1.pin3
  N5: Mod1.pin_5, J1.pin2
  N6: Mod1.pin_9, J1.pin1, R1.Pin_0
  N7: Mod1.pin_36, J1.pin7, R1.Pin_1
  N8: Mod1.pin_39, D1.cathode
  N9: Adafruit_DC_Power_BFF1.N$2, J1.pin6
  N10: Adafruit_DC_Power_BFF1.+5V, D1.anode

custom parts:
  Raspberry Pi Pico: Raspberry Pi Pico. Based around the RP2040 microcontroller the Pico is a low cost microcontroller device bringing Raspberry Pi quality, cost, and easy of use to the microcontroller space. Jan 2021, Split part in to two versions: tht (this one) and SMD. This one will drill holes for a .1 in header in pcb to allow plugging in the module as well as providing pads to solder the module to the top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
  Small signal Diode flat 300mil: Small signal diode such as the 1n4148 Footprint: mounted flat on 300mil centers.
